# Fritzing sketch neuroduino (saved by Fritzing 0.9.6b)
breadboards: 1

parts:
  Part1 = Arduino Leonardo (Rev3b)
  S7 = Pushbutton [package="[THT]"]
  R2 = Photocell (LDR) [package=THT]
  S9 = Pushbutton [package="[THT]"]
  S8 = Pushbutton [package="[THT]"]
  S6 = Pushbutton [package="[THT]"]
  R4 = Resistor [tolerance=±5% power=0.25 resistance=10k package=THT]
  U1 = BNC socket [package=bnc]
  U2 = BNC socket [package=bnc]
  U3 = BNC socket [package=bnc]
  U4 = BNC socket [package=bnc]

nets:
  N1: Part1.D4/A6, S6.Pin_1, S6.Pin_2
  N2: Part1.D5_PWM, S7.Pin_1, S7.Pin_2
  N3: Part1.D6_PWM/A7, S8.Pin_1, S8.Pin_2
  N4: Part1.D7, S9.Pin_1, S9.Pin_2
  N5: Part1.5V, R2.pin_0
  GND: Part1.GND, S7.Pin_3, S7.Pin_4, S9.Pin_3, S9.Pin_4, S8.Pin_3, S8.Pin_4, S6.Pin_3, S6.Pin_4, R4.Pin_1, U1.GND, U2.GND, U3.GND, U4.GND
  N6: Part1.A0, R2.pin_1, R4.Pin_0
  N7: Part1.D8/A8, U2.OUT
  N8: Part1.D9_PWM/A9, U1.OUT
  N9: Part1.D10_PWM/A10, U4.OUT
  N10: Part1.D11_PWM, U3.OUT
